# Fritzing sketch Pass Center (saved by Fritzing 0.9.3b)
breadboards: 1

parts:
  Componente1 = LCD1602-I2C
  Componente2 = RFID-RC522 [part_number=101218]
  S1 = Momentary Switch [package=ksa_sealed_tac_switch]
  R1 = Resistor [tolerance=±5% resistance=220 package="2010 [SMD]"]
  U1 = LuaNode32 / ESP32
  S2 = Momentary Switch [package=ksa_sealed_tac_switch]
  S3 = Momentary Switch [package=ksa_sealed_tac_switch]
  S4 = Momentary Switch [package=ksa_sealed_tac_switch]
  R2 = Resistor [tolerance=±5% resistance=220 package="2010 [SMD]"]
  R3 = Resistor [tolerance=±5% resistance=220 package="2010 [SMD]"]
  R4 = Resistor [tolerance=±5% resistance=220 package="2010 [SMD]"]
  SG1 = Buzzer 12mm [package=buzzer-12mm-ns]

nets:
  GND: Componente1.GND, Componente2.GND, U1.GND, R2.Pin_0, R3.Pin_0, R4.Pin_0, SG1.2
  VCC: Componente1.VCC, U1.Vin
  N1: Componente1.SDA, U1.D21
  N2: Componente1.SCL, U1.D22
  N3: Componente2.SDA, U1.D5
  N4: Componente2.SCK, U1.D18
  N5: Componente2.MOSI, U1.D23
  N6: Componente2.MISO, U1.D19
  N7: Componente2.RST, U1.VP
  3.3V: Componente2.3.3V, S1.2, U1.3V3, S2.2, S3.2, S4.2
  N8: S1.4, R1.Pin_1, U1.D2
  N9: U1.D27, SG1.1
  N10: U1.D14, S4.4, R4.Pin_1
  N11: U1.D12, S3.4, R3.Pin_1
  N12: U1.D13, S2.4, R2.Pin_1

custom parts:
  LCD1602-I2C: A standard character display, usually with 2x16 characters. Comes in many colors with LCM1602 IIC attached.
  LuaNode32 / ESP32: ESP32 based LuaNode32
